// Logisim project alu.circ as structural Verilog: 1 circuit, main circuit main
module main (
  input  [31:0] X,
  input  [31:0] Y,
  input  [3:0] Switch,
  output Signed_Overflow,
  output Equal,
  output [31:0] Result
);

  wire adder_2_cout, adder_3_cout, addOv, subOv, subtractor_2_bout, subtractor_3_bout;
  wire [0:0] Oslt, Osltu;
  wire [31:0] Oadd, Oaddu, Oand, Oor, Osll, Osra, Osrl, Osub, Osubu;

  Adder #(.width(32)) adder_1 (.a(X), .b(Y), .out(Oaddu));  // open: cin, cout
  Adder #(.width(31)) adder_2 (.a(X[30:0]), .b(Y[30:0]), .out(Oadd[30:0]), .cout(adder_2_cout));  // open: cin
  Adder #(.width(1)) adder_3 (.a(X[31]), .b(Y[31]), .out(Oadd[31]), .cin(adder_2_cout), .cout(adder_3_cout));
  xor xor_1 (addOv, adder_3_cout, adder_2_cout);
  Subtractor #(.width(32)) subtractor_1 (.a(X), .b(Y), .out(Osubu));  // open: bin, bout
  Subtractor #(.width(31)) subtractor_2 (
    .a(X[30:0]), .b(Y[30:0]), .out(Osub[30:0]), .bout(subtractor_2_bout));  // open: bin
  Subtractor #(.width(1)) subtractor_3 (
    .a(X[31]), .b(Y[31]), .out(Osub[31]), .bin(subtractor_2_bout), .bout(subtractor_3_bout));
  xor xor_2 (subOv, subtractor_3_bout, subtractor_2_bout);
  Comparator #(.width(32)) comparator_1 (.a(Osub), .b({32{1'b0}}), .eq(Equal));  // open: gt, lt
  Shifter #(.width(32)) shifter_1 (.in(Y), .\dist (X[4:0]), .out(Osll));
  Shifter #(.width(32), .shift("lr")) shifter_2 (.in(Y), .\dist (X[4:0]), .out(Osrl));
  Shifter #(.width(32), .shift("ar")) shifter_3 (.in(Y), .\dist (X[4:0]), .out(Osra));
  assign Oand = X & Y;  // AND_Gate and_1, 32 bits wide
  assign Oor = X | Y;  // OR_Gate or_1, 32 bits wide
  Comparator #(.width(32)) comparator_2 (.a(X), .b(Y), .lt(Oslt[0]));  // open: gt, eq
  Comparator #(.width(32), .mode("unsigned")) comparator_3 (.a(X), .b(Y), .lt(Osltu[0]));  // open: gt, eq
  Multiplexer #(.select(4)) multiplexer_1 (
    .in0(1'b0), .in1(1'b0), .in2(1'b0), .in5(addOv), .in6(1'b0), .in7(subOv), .in8(1'b0), .in9(1'b0),
    .in10(1'b0), .in11(1'b0), .in12(1'b0), .out(Signed_Overflow), .sel(Switch));  // open: in3, in4, in13, in14, in15, en
  Multiplexer #(.select(4), .width(32)) multiplexer_2 (
    .in0(Osll), .in1(Osrl), .in2(Osra), .in5(Oadd), .in6(Oaddu), .in7(Osub), .in8(Osubu), .in9(Oand),
    .in10(Oor), .in11({{31{1'b0}}, Oslt[0]}), .in12({{31{1'b0}}, Osltu[0]}), .out(Result), .sel(Switch));  // open: in3, in4, in13, in14, in15, en

  // Other names for the same wires on the sheet: overflow = Signed_Overflow; S[3:0] = Switch

  // Notes on the sheet:
  //   INPUTS to your circuit
  //   DON'T CHANGE THE LOCATIONS OF THE INPUTS AND OUTPUTS!
  //   OUTPUTS from your circuit
endmodule
