// Logisim project cpu.circ as structural Verilog: 3 circuits, main circuit main
module main (
  input  [31:0] INSTRUCTION,
  input  CLOCK,
  output [31:0] FETCH_ADDRESS,
  output [31:0] s0_Value,
  output [31:0] s1_Value,
  output [31:0] s2_Value,
  output [31:0] ra_Value,
  output [31:0] sp_Value,
  output [3:0] out_9
);

  wire ALUsrc, and_1_out, and_2_out, beq, bne, eq, ExtOp, j, jal, jr, LuiO, main_2_signed_overflow,
       main_3_p1, main_3_p2, main_3_p7, main_3_p11, main_3_p13, MemtoReg, MemWrite, nop, not_1_out, or_1_out,
       or_2_out, RegDst, RegWrite, shift, swinc;
  wire [3:0] adder_1_out_2;
  wire [4:0] multiplexer_1_out, multiplexer_2_out, multiplexer_3_out;
  wire [25:0] address;
  wire [27:0] adder_1_out, bit_extender_4_out, shifter_1_out;
  wire [31:0] adder_2_out, bit_extender_1_out, bit_extender_3_out, busA, busB, busW, immExt, main_2_result,
       main_3_p10, multiplexer_5_out, multiplexer_6_out, multiplexer_7_out, multiplexer_8_out,
       multiplexer_9_out, multiplexer_10_out, multiplexer_11_out, multiplexer_12_out, pc4, shifter_2_out,
       shifter_3_out, SignImm;
  wire [31:26] prev_instruction;

  Multiplexer #(.width(5)) multiplexer_1 (
    .in0(address[20:16]), .in1(address[15:11]), .out(multiplexer_1_out), .sel(RegDst));  // open: en
  Multiplexer #(.width(5)) multiplexer_2 (
    .in0(multiplexer_1_out), .in1(address[25:21]), .out(multiplexer_2_out), .sel(swinc));  // open: en
  Control control_1 (
    .in({prev_instruction, address}), .RegDst(RegDst), .ALUSrc(ALUsrc), .MemtoReg(MemtoReg),
    .RegWrite(RegWrite), .MemWrite(MemWrite), .J(j), .ExtOp(ExtOp), .luiO(LuiO), .swinc(swinc),
    .shift(shift), .jal(jal), .jr(jr), .beq(beq), .bne(bne), .ALUctr(out_9));
  Multiplexer #(.width(5)) multiplexer_3 (
    .in0(multiplexer_2_out), .in1({5{1'b1}}), .out(multiplexer_3_out), .sel(jal));  // open: en
  regfile_main main_1 (
    .Read_Register_1(address[25:21]), .Read_Register_2(address[20:16]), .Write_Register(multiplexer_3_out),
    .Write_Data(busW), .Write_Enable(RegWrite), .Clock(CLOCK), .Read_Data_1(busA), .Read_Data_2(busB),
    .s0_Value(s0_Value), .s1_Value(s1_Value), .s2_Value(s2_Value), .ra_Value(ra_Value), .sp_Value(sp_Value));
  assign bit_extender_1_out = {{16{1'b0}}, address[15:0]};  // Bit_Extender bit_extender_1
  assign SignImm = {{16{address[15]}}, address[15:0]};  // Bit_Extender bit_extender_2
  assign bit_extender_3_out = {{27{1'b0}}, address[10:6]};  // Bit_Extender bit_extender_3
  Multiplexer #(.width(32)) multiplexer_4 (
    .in0(bit_extender_1_out), .in1(SignImm), .out(immExt), .sel(ExtOp));  // open: en
  assign bit_extender_4_out = {{2{address[25]}}, address};  // Bit_Extender bit_extender_4
  LED led_1 (.in(main_2_signed_overflow));
  Multiplexer #(.width(32)) multiplexer_5 (
    .in0(busA), .in1(bit_extender_3_out), .out(multiplexer_5_out), .sel(shift));  // open: en
  Multiplexer #(.width(32)) multiplexer_6 (
    .in0(busB), .in1(immExt), .out(multiplexer_6_out), .sel(ALUsrc));  // open: en
  Shifter #(.width(28)) shifter_1 (.in(bit_extender_4_out), .\dist (5'b00010), .out(shifter_1_out));
  alu_main main_2 (
    .Switch(out_9), .X(multiplexer_5_out), .Equal(eq), .Result(main_2_result),
    .Signed_Overflow(main_2_signed_overflow), .Y(multiplexer_6_out));
  Adder #(.width(32)) adder_1 (.a(32'h4), .b(FETCH_ADDRESS), .out({adder_1_out_2, adder_1_out}));  // open: cin, cout
  Register #(.width(32)) PC__Delay (.D({adder_1_out_2, adder_1_out}), .Q(pc4), .clk(CLOCK));  // open: en, clr
  Multiplexer #(.width(32)) multiplexer_7 (
    .in0({adder_1_out_2, adder_1_out}), .in1({adder_1_out_2, shifter_1_out}), .out(multiplexer_7_out),
    .sel(or_1_out));  // open: en
  or or_1 (or_1_out, j, jal);
  Shifter #(.width(32)) shifter_2 (.in(SignImm), .\dist (5'b00010), .out(shifter_2_out));
  Adder #(.width(32)) adder_2 (.a(pc4), .b(shifter_2_out), .out(adder_2_out));  // open: cin, cout
  or or_2 (or_2_out, and_1_out, and_2_out);
  and and_1 (and_1_out, eq, beq);
  Multiplexer #(.width(32)) multiplexer_8 (
    .in0(main_2_result), .in1(shifter_3_out), .out(multiplexer_8_out), .sel(LuiO));  // open: en
  Shifter #(.width(32)) shifter_3 (.in(immExt), .\dist (5'b10000), .out(shifter_3_out));
  // mem_main main_3: pin names not known; wires that end beside it: main_3_p1, main_3_p2, main_3_p2, main_2_result, busB, MemWrite, main_3_p7, CLOCK, main_3_p7, main_3_p10, main_3_p11, main_3_p11, main_3_p13, main_3_p13, main_3_p1
  Multiplexer #(.width(32)) multiplexer_9 (
    .in0(multiplexer_7_out), .in1(adder_2_out), .out(multiplexer_9_out), .sel(or_2_out));  // open: en
  and and_2 (and_2_out, not_1_out, bne);
  not not_1 (not_1_out, eq);
  Multiplexer #(.width(32)) multiplexer_10 (
    .in0(multiplexer_8_out), .in1(pc4), .out(multiplexer_10_out), .sel(jal));  // open: en
  Multiplexer #(.width(32)) multiplexer_11 (
    .in0(INSTRUCTION), .in1({32{1'b0}}), .out(multiplexer_11_out), .sel(nop));  // open: en
  Multiplexer #(.width(32)) multiplexer_12 (
    .in0(multiplexer_9_out), .in1(busA), .out(multiplexer_12_out), .sel(jr));  // open: en
  Multiplexer #(.width(32)) multiplexer_13 (
    .in0(multiplexer_10_out), .in1(main_3_p10), .out(busW), .sel(MemtoReg));  // open: en
  Register #(.width(32)) pipeline (
    .D(multiplexer_11_out), .Q({prev_instruction, address}), .clk(CLOCK));  // open: en, clr
  Register #(.width(32)) PC (.D(multiplexer_12_out), .Q(FETCH_ADDRESS), .clk(CLOCK));  // open: en, clr
  or or_3 (nop, or_2_out, jr, j, jal);

  // Other names for the same wires on the sheet: ALUctr[3:0] = out_9; clk = CLOCK; fetch_addr[31:0] = FETCH_ADDRESS;
  //   imm[15:0] = address[15:0]; prev_instruction[25:0] = address; shamt[4:0] = address[10:6];
  //   rd[4:0] = address[15:11]; rt[4:0] = address[20:16]; rs[4:0] = address[25:21]; ra[31:0] = ra_Value;
  //   s0[31:0] = s0_Value; s1[31:0] = s1_Value; s2[31:0] = s2_Value; sp[31:0] = sp_Value

  // Notes on the sheet:
  //   Output
  //   These are outputs/inputs from run.circ
  //   Inputs
  //   These are DEBUG/TEST outputs from your circuit.
endmodule

module Control2 (
  input  [31:0] in,
  output [11:0] out_2,
  output out_3,
  output out_4,
  output out_5,
  output out_6,
  output out_7,
  output out_8,
  output out_9,
  output out_10,
  output [3:0] out_11,
  output swinc
);

  wire undriven;
  wire [11:0] multiplexer_1_out, multiplexer_3_out, multiplexer_4_out, multiplexer_5_out;
  wire [31:0] shifter_1_out;

  Shifter #(.width(32)) shifter_1 (.in(in), .\dist (5'b11010), .out(shifter_1_out));
  Multiplexer #(.select(5), .width(12)) multiplexer_1 (
    .in0(12'h90), .in3(12'h290), .out(multiplexer_1_out), .sel(in[4:0]));  // open: in1, in2, in4, in5, in6, in7, in8, in9, in10, in11, in12, in13, in14, in15, in16, in17, in18, in19, in20, in21, in22, in23, in24, in25, in26, in27, in28, in29, in30, in31, en
  Multiplexer #(.width(12)) multiplexer_2 (
    .in0(multiplexer_1_out), .in1(multiplexer_3_out), .out(out_2), .sel(in[5]), .en(undriven));
  Multiplexer #(.select(5), .width(12)) multiplexer_3 (
    .in0(12'h590), .in1(12'h690), .in4(12'h990), .in5(12'ha90), .in10(12'hb90), .in11(12'hc90),
    .out(multiplexer_3_out), .sel(in[4:0]));  // open: in2, in3, in6, in7, in8, in9, in12, in13, in14, in15, in16, in17, in18, in19, in20, in21, in22, in23, in24, in25, in26, in27, in28, in29, in30, in31, en
  Multiplexer #(.select(5), .width(12)) multiplexer_4 (
    .in0(out_2), .in1(out_2), .out(multiplexer_4_out), .sel(shifter_1_out[4:0]));  // open: in2, in3, in4, in5, in6, in7, in8, in9, in10, in11, in12, in13, in14, in15, in16, in17, in18, in19, in20, in21, in22, in23, in24, in25, in26, in27, in28, in29, in30, in31, en
  Multiplexer #(.select(5), .width(12)) multiplexer_5 (
    .out(multiplexer_5_out), .sel(shifter_1_out[4:0]));  // open: in0, in1, in2, in3, in4, in5, in6, in7, in8, in9, in10, in11, in12, in13, in14, in15, in16, in17, in18, in19, in20, in21, in22, in23, in24, in25, in26, in27, in28, in29, in30, in31, en
  Multiplexer #(.width(12)) multiplexer_6 (
    .in0(multiplexer_4_out), .in1(multiplexer_5_out),
    .out({out_11, out_10, out_9, out_8, out_7, out_6, out_5, out_4, out_3}), .sel(shifter_1_out[5]));  // open: en
endmodule

module Control (
  input  [31:0] in,
  output RegDst,
  output ALUSrc,
  output MemtoReg,
  output RegWrite,
  output MemWrite,
  output J,
  output ExtOp,
  output luiO,
  output swinc,
  output shift,
  output jal,
  output jr,
  output beq,
  output bne,
  output [3:0] ALUctr
);

  wire add, addi, addiu, addu, \and , andi, comparator_16_eq, comparator_17_eq, comparator_18_eq,
       comparator_19_eq, comparator_20_eq, comparator_21_eq, comparator_22_eq, comparator_23_eq,
       comparator_24_eq, comparator_25_eq, comparator_26_eq, comparator_27_eq, \or , or_1_out, or_2_out,
       or_3_out, or_4_out, or_6_out, or_7_out, ori, sll, slt, slti, sltiu, sltu, sra, srl, sub, subu, sw;
  wire [3:0] multiplexer_1_out, multiplexer_2_out, multiplexer_3_out, multiplexer_4_out, multiplexer_5_out,
       multiplexer_6_out, multiplexer_7_out, multiplexer_8_out, multiplexer_9_out;

  Comparator #(.width(6), .mode("unsigned")) comparator_1 (.a(in[31:26]), .b({6{1'b0}}), .eq(RegDst));  // open: gt, lt
  Comparator #(.width(6), .mode("unsigned")) comparator_2 (.a(in[31:26]), .b(6'b001000), .eq(addi));  // open: gt, lt
  Comparator #(.width(6), .mode("unsigned")) comparator_3 (.a(in[31:26]), .b(6'b001001), .eq(addiu));  // open: gt, lt
  Comparator #(.width(6), .mode("unsigned")) comparator_4 (.a(in[31:26]), .b(6'b001100), .eq(andi));  // open: gt, lt
  Comparator #(.width(6), .mode("unsigned")) comparator_5 (.a(in[31:26]), .b(6'b000100), .eq(beq));  // open: gt, lt
  Comparator #(.width(6), .mode("unsigned")) comparator_6 (.a(in[31:26]), .b(6'b000101), .eq(bne));  // open: gt, lt
  Comparator #(.width(6), .mode("unsigned")) comparator_7 (.a(in[31:26]), .b(6'b000010), .eq(J));  // open: gt, lt
  Comparator #(.width(6), .mode("unsigned")) comparator_8 (.a(in[31:26]), .b(6'b000011), .eq(jal));  // open: gt, lt
  Comparator #(.width(6), .mode("unsigned")) comparator_9 (.a(in[31:26]), .b(6'b001111), .eq(luiO));  // open: gt, lt
  Comparator #(.width(6), .mode("unsigned")) comparator_10 (
    .a(in[31:26]), .b(6'b100011), .eq(MemtoReg));  // open: gt, lt
  Comparator #(.width(6), .mode("unsigned")) comparator_11 (.a(in[31:26]), .b(6'b001101), .eq(ori));  // open: gt, lt
  Comparator #(.width(6), .mode("unsigned")) comparator_12 (.a(in[31:26]), .b(6'b001010), .eq(slti));  // open: gt, lt
  Comparator #(.width(6), .mode("unsigned")) comparator_13 (.a(in[31:26]), .b(6'b001011), .eq(sltiu));  // open: gt, lt
  Comparator #(.width(6), .mode("unsigned")) comparator_14 (.a(in[31:26]), .b(6'b101011), .eq(sw));  // open: gt, lt
  Comparator #(.width(6), .mode("unsigned")) comparator_15 (.a(in[31:26]), .b(6'b101100), .eq(swinc));  // open: gt, lt
  Comparator #(.width(6), .mode("unsigned")) comparator_16 (
    .a(in[5:0]), .b(6'b100000), .eq(comparator_16_eq));  // open: gt, lt
  Comparator #(.width(6), .mode("unsigned")) comparator_17 (
    .a(in[5:0]), .b(6'b000010), .eq(comparator_17_eq));  // open: gt, lt
  Comparator #(.width(6), .mode("unsigned")) comparator_18 (
    .a(in[5:0]), .b(6'b000011), .eq(comparator_18_eq));  // open: gt, lt
  Comparator #(.width(6), .mode("unsigned")) comparator_19 (
    .a(in[5:0]), .b(6'b100001), .eq(comparator_19_eq));  // open: gt, lt
  Comparator #(.width(6), .mode("unsigned")) comparator_20 (
    .a(in[5:0]), .b(6'b100010), .eq(comparator_20_eq));  // open: gt, lt
  Comparator #(.width(6), .mode("unsigned")) comparator_21 (
    .a(in[5:0]), .b(6'b100011), .eq(comparator_21_eq));  // open: gt, lt
  Comparator #(.width(6), .mode("unsigned")) comparator_22 (
    .a(in[5:0]), .b(6'b100100), .eq(comparator_22_eq));  // open: gt, lt
  Comparator #(.width(6), .mode("unsigned")) comparator_23 (
    .a(in[5:0]), .b(6'b100101), .eq(comparator_23_eq));  // open: gt, lt
  Comparator #(.width(6), .mode("unsigned")) comparator_24 (
    .a(in[5:0]), .b(6'b101010), .eq(comparator_24_eq));  // open: gt, lt
  Comparator #(.width(6), .mode("unsigned")) comparator_25 (
    .a(in[5:0]), .b(6'b101011), .eq(comparator_25_eq));  // open: gt, lt
  Comparator #(.width(6), .mode("unsigned")) comparator_26 (
    .a(in[5:0]), .b(6'b001000), .eq(comparator_26_eq));  // open: gt, lt
  Comparator #(.width(6), .mode("unsigned")) comparator_27 (
    .a(in[5:0]), .b({6{1'b0}}), .eq(comparator_27_eq));  // open: gt, lt
  and and_1 (add, RegDst, comparator_16_eq);
  and and_2 (srl, RegDst, comparator_17_eq);
  and and_3 (sra, RegDst, comparator_18_eq);
  and and_4 (addu, RegDst, comparator_19_eq);
  and and_5 (sub, RegDst, comparator_20_eq);
  and and_6 (subu, RegDst, comparator_21_eq);
  and and_7 (\and , RegDst, comparator_22_eq);
  and and_8 (\or , RegDst, comparator_23_eq);
  and and_9 (slt, RegDst, comparator_24_eq);
  and and_10 (sltu, RegDst, comparator_25_eq);
  and and_11 (jr, RegDst, comparator_26_eq);
  and and_12 (sll, RegDst, comparator_27_eq);
  Multiplexer #(.width(4)) multiplexer_1 (
    .in0(4'b0000), .in1(4'b0001), .out(multiplexer_1_out), .sel(srl));  // open: en
  Multiplexer #(.width(4)) multiplexer_2 (
    .in0(multiplexer_1_out), .in1(4'b0010), .out(multiplexer_2_out), .sel(sra));  // open: en
  Multiplexer #(.width(4)) multiplexer_3 (
    .in0(multiplexer_2_out), .in1(4'b0101), .out(multiplexer_3_out), .sel(or_1_out));  // open: en
  Multiplexer #(.width(4)) multiplexer_4 (
    .in0(multiplexer_3_out), .in1(4'b0110), .out(multiplexer_4_out), .sel(or_2_out));  // open: en
  or or_1 (or_1_out, add, addi);
  or or_2 (or_2_out, sw, addu, swinc, addiu, MemtoReg);
  Multiplexer #(.width(4)) multiplexer_5 (
    .in0(multiplexer_4_out), .in1(4'b0111), .out(multiplexer_5_out), .sel(sub));  // open: en
  Multiplexer #(.width(4)) multiplexer_6 (
    .in0(multiplexer_5_out), .in1(4'b1000), .out(multiplexer_6_out), .sel(subu));  // open: en
  Multiplexer #(.width(4)) multiplexer_7 (
    .in0(multiplexer_6_out), .in1(4'b1001), .out(multiplexer_7_out), .sel(or_4_out));  // open: en
  Multiplexer #(.width(4)) multiplexer_8 (
    .in0(multiplexer_7_out), .in1(4'b1010), .out(multiplexer_8_out), .sel(or_3_out));  // open: en
  or or_3 (or_3_out, \or , ori);
  or or_4 (or_4_out, \and , andi);
  or or_5 (RegWrite, RegDst, addi, addiu, andi, luiO, MemtoReg, ori, slti, sltiu, swinc, jal);
  Multiplexer #(.width(4)) multiplexer_9 (
    .in0(multiplexer_8_out), .in1(4'b1011), .out(multiplexer_9_out), .sel(or_7_out));  // open: en
  Multiplexer #(.width(4)) multiplexer_10 (
    .in0(multiplexer_9_out), .in1(4'b1100), .out(ALUctr), .sel(or_6_out));  // open: en
  or or_6 (or_6_out, sltu, sltiu);
  or or_7 (or_7_out, slt, slti);
  nor nor_1 (ALUSrc, RegDst, beq, bne);
  or or_8 (MemWrite, sw, swinc);
  nor nor_2 (ExtOp, andi, ori);
  or or_9 (shift, sll, srl, sra);

  // Other names for the same wires on the sheet: funcO[5:0] = in[5:0]; opcode[5:0] = in[31:26]; lui = luiO;
  //   lw = MemtoReg; rtype = RegDst
endmodule
