// Logisim project regfile.circ as structural Verilog: 1 circuit, main circuit main
module main (
  input  [4:0] Read_Register_1,
  input  [4:0] Read_Register_2,
  input  [4:0] Write_Register,
  input  [31:0] Write_Data,
  input  Write_Enable,
  input  Clock,
  output [31:0] s0_Value,
  output [31:0] s1_Value,
  output [31:0] s2_Value,
  output [31:0] ra_Value,
  output [31:0] sp_Value,
  output [31:0] Read_Data_1,
  output [31:0] Read_Data_2
);

  wire [31:0] a0, a1, a2, a3, at, fp, gp, k0, k1, s3, s4, s5, s6, s7, t0, t1, t2, t3, t4, t5, t6, t7, t8, t9,
       v0, v1, Wa0, Wa1, Wa2, Wa3, Wat, Wfp, Wgp, Wk0, Wk1, Wra, Ws0, Ws1, Ws2, Ws3, Ws4, Ws5, Ws6, Ws7, Wsp,
       Wt0, Wt1, Wt2, Wt3, Wt4, Wt5, Wt6, Wt7, Wt8, Wt9, Wv0, Wv1;

  Demultiplexer #(.select(5), .width(32), .tristate("true")) demultiplexer_1 (
    .out1(Wat), .out2(Wv0), .out3(Wv1), .out4(Wa0), .out5(Wa1), .out6(Wa2), .out7(Wa3), .out8(Wt0),
    .out9(Wt1), .out10(Wt2), .out11(Wt3), .out12(Wt4), .out13(Wt5), .out14(Wt6), .out15(Wt7), .out16(Ws0),
    .out17(Ws1), .out18(Ws2), .out19(Ws3), .out20(Ws4), .out21(Ws5), .out22(Ws6), .out23(Ws7), .out24(Wt8),
    .out25(Wt9), .out26(Wk0), .out27(Wk1), .out28(Wgp), .out29(Wsp), .out30(Wfp), .out31(Wra),
    .in(Write_Data), .sel(Write_Register));  // open: out0, en
  Register #(.width(32)) register_1 (.D(Wat), .Q(at), .clk(Clock));  // open: en, clr
  Register #(.width(32)) register_2 (.D(Wa1), .en(Write_Enable), .Q(a1), .clk(Clock));  // open: clr
  Register #(.width(32)) register_3 (.D(Wt1), .en(Write_Enable), .Q(t1), .clk(Clock));  // open: clr
  Register #(.width(32)) register_4 (.D(Wt5), .en(Write_Enable), .Q(t5), .clk(Clock));  // open: clr
  Register #(.width(32)) register_5 (.D(Ws1), .en(Write_Enable), .Q(s1_Value), .clk(Clock));  // open: clr
  Register #(.width(32)) register_6 (.D(Wt9), .en(Write_Enable), .Q(t9), .clk(Clock));  // open: clr
  Register #(.width(32)) register_7 (.D(Wv0), .en(Write_Enable), .Q(v0), .clk(Clock));  // open: clr
  Register #(.width(32)) register_8 (.D(Wa2), .en(Write_Enable), .Q(a2), .clk(Clock));  // open: clr
  Register #(.width(32)) register_9 (.D(Wt2), .en(Write_Enable), .Q(t2), .clk(Clock));  // open: clr
  Register #(.width(32)) register_10 (.D(Wt6), .en(Write_Enable), .Q(t6), .clk(Clock));  // open: clr
  Register #(.width(32)) register_11 (.D(Ws2), .en(Write_Enable), .Q(s2_Value), .clk(Clock));  // open: clr
  Register #(.width(32)) register_12 (.D(Wk0), .en(Write_Enable), .Q(k0), .clk(Clock));  // open: clr
  Register #(.width(32)) register_13 (.D(Wv1), .en(Write_Enable), .Q(v1), .clk(Clock));  // open: clr
  Register #(.width(32)) register_14 (.D(Wa3), .en(Write_Enable), .Q(a3), .clk(Clock));  // open: clr
  Register #(.width(32)) register_15 (.D(Wt3), .en(Write_Enable), .Q(t3), .clk(Clock));  // open: clr
  Register #(.width(32)) register_16 (.D(Wt7), .en(Write_Enable), .Q(t7), .clk(Clock));  // open: clr
  Register #(.width(32)) register_17 (.D(Ws3), .en(Write_Enable), .Q(s3), .clk(Clock));  // open: clr
  Register #(.width(32)) register_18 (.D(Wk1), .en(Write_Enable), .Q(k1), .clk(Clock));  // open: clr
  Register #(.width(32)) register_19 (.D(Wa0), .en(Write_Enable), .Q(a0), .clk(Clock));  // open: clr
  Register #(.width(32)) register_20 (.D(Wt0), .en(Write_Enable), .Q(t0), .clk(Clock));  // open: clr
  Register #(.width(32)) register_21 (.D(Wt4), .en(Write_Enable), .Q(t4), .clk(Clock));  // open: clr
  Register #(.width(32)) register_22 (.D(Ws0), .en(Write_Enable), .Q(s0_Value), .clk(Clock));  // open: clr
  Register #(.width(32)) register_23 (.D(Ws4), .en(Write_Enable), .Q(s4), .clk(Clock));  // open: clr
  Register #(.width(32)) register_24 (.D(Wgp), .en(Write_Enable), .Q(gp), .clk(Clock));  // open: clr
  Register #(.width(32)) register_25 (.D(Ws5), .en(Write_Enable), .Q(s5), .clk(Clock));  // open: clr
  Register #(.width(32)) register_26 (.D(Wsp), .en(Write_Enable), .Q(sp_Value), .clk(Clock));  // open: clr
  Multiplexer #(.select(5), .width(32)) multiplexer_1 (
    .in0({32{1'b0}}), .in1(at), .in2(v0), .in3(v1), .in4(a0), .in5(a1), .in6(a2), .in7(a3), .in8(t0),
    .in9(t1), .in10(t2), .in11(t3), .in12(t4), .in13(t5), .in14(t6), .in15(t7), .in16(s0_Value),
    .in17(s1_Value), .in18(s2_Value), .in19(s3), .in20(s4), .in21(s5), .in22(s6), .in23(s7), .in24(t8),
    .in25(t9), .in26(k0), .in27(k1), .in28(gp), .in29(sp_Value), .in30(fp), .in31(ra_Value),
    .out(Read_Data_1), .sel(Read_Register_1));  // open: en
  Register #(.width(32)) register_27 (.D(Ws6), .en(Write_Enable), .Q(s6), .clk(Clock));  // open: clr
  Register #(.width(32)) register_28 (.D(Wfp), .en(Write_Enable), .Q(fp), .clk(Clock));  // open: clr
  Register #(.width(32)) register_29 (.D(Ws7), .en(Write_Enable), .Q(s7), .clk(Clock));  // open: clr
  Register #(.width(32)) register_30 (.D(Wra), .en(Write_Enable), .Q(ra_Value), .clk(Clock));  // open: clr
  Register #(.width(32)) register_31 (.D(Wt8), .en(Write_Enable), .Q(t8), .clk(Clock));  // open: clr
  Multiplexer #(.select(5), .width(32)) multiplexer_2 (
    .in0({32{1'b0}}), .in1(at), .in2(v0), .in3(v1), .in4(a0), .in5(a1), .in6(a2), .in7(a3), .in8(t0),
    .in9(t1), .in10(t2), .in11(t3), .in12(t4), .in13(t5), .in14(t6), .in15(t7), .in16(s0_Value),
    .in17(s1_Value), .in18(s2_Value), .in19(s3), .in20(s4), .in21(s5), .in22(s6), .in23(s7), .in24(t8),
    .in25(t9), .in26(k0), .in27(k1), .in28(gp), .in29(sp_Value), .in30(fp), .in31(ra_Value),
    .out(Read_Data_2), .sel(Read_Register_2));  // open: en

  // Other names for the same wires on the sheet: clk = Clock; ra[31:0] = ra_Value; read_data1[31:0] = Read_Data_1;
  //   read_data2[31:0] = Read_Data_2; read_reg1[4:0] = Read_Register_1; read_reg2[4:0] = Read_Register_2;
  //   s0[31:0] = s0_Value; s1[31:0] = s1_Value; s2[31:0] = s2_Value; sp[31:0] = sp_Value; write_en = Write_Enable;
  //   write_reg[4:0] = Write_Register

  // Notes on the sheet:
  //   INPUTS to your circuit
  //   DON'T CHANGE THE LOCATIONS OF THE INPUTS AND OUTPUTS!
  //   These are DEBUG/TEST outputs from your circuit.
  //   OUTPUTS from your circuit
endmodule
