// Logisim project CPU-starter_kit_test.circ as structural Verilog: 1 circuit, main circuit main
module main (
  output [31:0] s0_Value,
  output [31:0] s1_Value,
  output [31:0] s2_Value,
  output [31:0] ra_Value,
  output [31:0] sp_Value,
  output [31:0] Time_Step,
  output [31:0] Requested_Address,
  output [31:0] Requested_Instruction,
  output halt
);

  wire clock_1_out, comparator_1_eq, comparator_2_eq;
  wire [31:0] register_1_q;

  Clock clock_1 (.out(clock_1_out));
  cpu_main main_1 (
    .INSTRUCTION(Requested_Instruction), .CLOCK(clock_1_out), .FETCH_ADDRESS(Requested_Address),
    .s0_Value(s0_Value), .s1_Value(s1_Value), .s2_Value(s2_Value), .ra_Value(ra_Value), .sp_Value(sp_Value));
  Counter #(.width(32), .max('hffffffff)) counter_1 (
    .Q(Time_Step), .clk(clock_1_out));  // open: load, D, count, carry, clr
  Register #(.width(32)) register_1 (.D(Requested_Instruction), .Q(register_1_q), .clk(clock_1_out));  // open: en, clr
  Comparator #(.width(32)) comparator_1 (
    .a(Requested_Instruction), .b(register_1_q), .eq(comparator_1_eq));  // open: gt, lt
  Comparator #(.width(32)) comparator_2 (
    .a(Requested_Instruction), .b({32{1'b0}}), .eq(comparator_2_eq));  // open: gt, lt
  and and_1 (halt, comparator_1_eq, comparator_2_eq);
  // Probe on Requested_Address
  ROM #(.addrWidth(24), .dataWidth(32)) rom_1 (
    .addr(Requested_Address[25:2]), .data(Requested_Instruction));  // open: sel
  // Probe on Requested_Instruction

  // Other names for the same wires on the sheet: fetch_addr[31:0] = Requested_Address;
  //   Instruction[31:0] = Requested_Instruction

  // Notes on the sheet:
  //   YOUR CPU SHOULD FIT IN HERE!
  //   Instruction Memory
  //   contents of rom_1 (hex, n*v repeats v):
  //   201d3ffc 20100010 24113000 ae300000 2010000f ae300004 8e320000 8e320004
endmodule
